# Fritzing sketch fritzing (saved by Fritzing 0.9.3b)
breadboards: 1

parts:
  LLC1 = Logic Level Converter [package="Breakout board"]
  LLC2 = Logic Level Converter [package="Breakout board"]
  LCD1 = 2.8" SPI TFT Module [part_number=MSP2807]
  J1 = Piezo Speaker
  LED1 = smd LED [color="Red (633nm)" package="0805 [SMD]"]
  R1 = Resistor [tolerance=±5% resistance=220 package=THT]

nets:
  N1: LLC1.LV1, LCD1.pin7
  N2: LLC1.LV2, LCD1.pin9
  N3: LLC1.LV, LLC2.LV
  N4: LLC1.L-GND, LLC1.H-GND, LLC2.L-GND, LLC2.H-GND, LCD1.pin2, J1.pin1, LED1.cathode
  N5: LLC1.HV, LLC2.HV, LCD1.pin1, LCD1.pin8
  N6: LLC2.LV1, LCD1.pin3
  N7: LLC2.LV2, LCD1.pin4
  N8: LLC2.LV3, LCD1.pin5
  N9: LLC2.LV4, LCD1.pin6
  N10: LED1.anode, R1.Pin_0

notes:
  5V
  GND
  3.3V
  As shown below, connect LattePanda Alpha GPIO pins to the 3.5" 320x480 TFT LCD Touch Screen via High-Level pins on bi-directional logic level converters, the buzzer, and the 5mm green LED.
  // Connections
  // LattePanda Alpha 864s (Arduino Leonardo) :
  // 3.5'' 320x480 TFT LCD Touch Screen (ILI9488)
  // D10 -------------------------- CS
  // D8 --------------------------- RESET
  // D9 --------------------------- D/C
  // MOSI ------------------------ SDI
  // SCK -------------------------- SCK
  // MISO ------------------------ SDO(MISO)
  // Buzzer
  // D11 --------------------------- S
  // 5mm Green LED
  // D12 --------------------------- S

custom parts:
  Logic Level Converter: 5V to/from 3.3V logic level converter
  2.8" SPI TFT Module: A generic 2.8 inch LCD TFT 320x240 display with touchscreen and SD card slot. Uses the ILI9341 controller, like the Adafruit displays of this size uses.
